# Fritzing sketch lock (saved by Fritzing 0.9.3b)
circuit board: 8.4675cm x 8.48766cm
breadboards: 1

parts:
  元件1 = Arduino Nano (Rev3.0)
  hc-sr1 = hc-sr04
  元件2 = Bluetooth HC-05 Macho
  元件3 = Max Power IR LED Kit
  元件4 = RFID-RC522-v2
  U1 = Barometric Pressure Sensor

nets:
  N1: 元件1.D1/TX, 元件2.RXD
  N2: 元件1.D0/RX, 元件2.TXD
  GND: 元件1.GND, hc-sr1.GND, 元件2.GND, 元件3.GND, 元件4.GND
  N3: 元件1.D2, hc-sr1.Trig
  N4: 元件1.D3, hc-sr1.Echo
  N5: 元件1.D4, 元件3.CONTROL
  N6: 元件1.D5, U1.IN4
  N7: 元件1.D6, U1.IN3
  N8: 元件1.D7, U1.IN2
  N9: 元件1.D8, U1.IN1
  N10: 元件1.D9, 元件4.RST
  N11: 元件1.D10, 元件4.SDA
  N12: 元件1.D11/MOSI, 元件4.MOSI
  N13: 元件1.D12/MISO, 元件4.MISO
  VCC: 元件1.5V, hc-sr1.VCC, 元件2.VCC, 元件3.VCC
  3V3: 元件1.3V3, 元件4.3.3V
  N14: 元件1.D13/SCK, 元件4.SCK

custom parts:
  RFID-RC522-v2: A simple China made RFID-RC522 Reader; do check the pin labels, as this is a MFRC522 based clone.
  Barometric Pressure Sensor: SCP1000 Barometric Pressure sensor. Can sense air pressure and temperature. SPI interface.
